# Fritzing sketch 74hc595 (saved by Fritzing 0.9.3b)
breadboards: 1

parts:
  Raspberry_Pi_1 = Raspberry Pi 3 [part_number=RPI-3-V1.2]
  U1 = 74HC595 [package="DIP16 [THT]"]
  R1 = Resistor [tolerance=±5% resistance=220 package=THT]
  R2 = Resistor [tolerance=±5% resistance=220 package=THT]
  R3 = Resistor [tolerance=±5% resistance=220 package=THT]
  R4 = Resistor [tolerance=±5% resistance=220 package=THT]
  R5 = Resistor [tolerance=±5% resistance=220 package=THT]
  R6 = Resistor [tolerance=±5% resistance=220 package=THT]
  R7 = Resistor [tolerance=±5% resistance=220 package=THT]
  R8 = Resistor [tolerance=±5% resistance=220 package=THT]
  LED1 = LED - 5mm [color="Red (633nm)" package="5 mm [THT]"]
  LED2 = LED - 5mm [color="Red (633nm)" package="5 mm [THT]"]
  LED3 = LED - 5mm [color="Red (633nm)" package="5 mm [THT]"]
  LED4 = LED - 5mm [color="Red (633nm)" package="5 mm [THT]"]
  LED5 = LED - 5mm [color="Red (633nm)" package="5 mm [THT]"]
  LED6 = LED - 5mm [color="Red (633nm)" package="5 mm [THT]"]
  LED7 = LED - 5mm [color="Red (633nm)" package="5 mm [THT]"]
  LED8 = LED - 5mm [color="Red (633nm)" package="5 mm [THT]"]

nets:
  N1: Raspberry_Pi_1.GIPO17, U1.DS
  N2: Raspberry_Pi_1.GIPO27, U1.SH_CP
  N3: Raspberry_Pi_1.GIPO18, U1.ST_CP
  N4: U1.Q1, R2.Pin_0
  N5: U1.Q2, R3.Pin_0
  N6: U1.Q3, R4.Pin_0
  N7: U1.Q4, R5.Pin_0
  N8: U1.Q5, R6.Pin_0
  N9: U1.Q6, R7.Pin_0
  N10: U1.Q7, R8.Pin_0
  N11: U1.GND, U1.OE, LED1.cathode, LED2.cathode, LED3.cathode, LED4.cathode, LED5.cathode, LED6.cathode, LED7.cathode, LED8.cathode
  N12: U1.MR, U1.VCC
  N13: U1.Q0, R1.Pin_0
  N14: R1.Pin_1, LED8.anode
  N15: R2.Pin_1, LED6.anode
  N16: R3.Pin_1, LED7.anode
  N17: R4.Pin_1, LED3.anode
  N18: R5.Pin_1, LED4.anode
  N19: R6.Pin_1, LED5.anode
  N20: R7.Pin_1, LED2.anode
  N21: R8.Pin_1, LED1.anode
