# Fritzing sketch ldr (saved by Fritzing 0.9.3b)
breadboards: 1

parts:
  Raspberry_Pi_1 = Raspberry Pi 3 [part_number=RPI-3-V1.2]
  C1 = Electrolytic Capacitor [capacitance=10µF voltage=50V package="100 mil [THT, electrolytic]"]
  R1 = Photocell (LDR) [package=THT]

nets:
  N1: Raspberry_Pi_1.3v3, R1.pin_0
  N2: Raspberry_Pi_1.GIPO18, C1.+, R1.pin_1
  N3: Raspberry_Pi_1.GND, C1.-
