# Fritzing sketch charlieplexing_6 (saved by Fritzing 0.9.3b)
breadboards: 1

parts:
  Raspberry_Pi_1 = Raspberry Pi 3 [part_number=RPI-3-V1.2]
  LED1 = LED - 5mm [color="Red (633nm)" package="5 mm [THT]"]
  R1 = Resistor [tolerance=±5% resistance=220 package=THT]
  LED2 = LED - 5mm [color="Red (633nm)" package="5 mm [THT]"]
  LED3 = LED - 5mm [color="Red (633nm)" package="5 mm [THT]"]
  LED4 = LED - 5mm [color="Red (633nm)" package="5 mm [THT]"]
  LED5 = LED - 5mm [color="Red (633nm)" package="5 mm [THT]"]
  LED6 = LED - 5mm [color="Red (633nm)" package="5 mm [THT]"]
  R2 = Resistor [tolerance=±5% resistance=220 package=THT]
  LED7 = LED - 5mm [color="Red (633nm)" package="5 mm [THT]"]
  R3 = Resistor [tolerance=±5% resistance=220 package=THT]
  LED8 = LED - 5mm [color="Red (633nm)" package="5 mm [THT]"]
  LED9 = LED - 5mm [color="Red (633nm)" package="5 mm [THT]"]
  LED10 = LED - 5mm [color="Red (633nm)" package="5 mm [THT]"]
  LED11 = LED - 5mm [color="Red (633nm)" package="5 mm [THT]"]
  LED12 = LED - 5mm [color="Red (633nm)" package="5 mm [THT]"]
  R4 = Resistor [tolerance=±5% resistance=220 package=THT]

nets:
  N1: Raspberry_Pi_1.GIPO26, R3.Pin_0
  N2: Raspberry_Pi_1.GIPO21, R2.Pin_0
  N3: Raspberry_Pi_1.GIPO20, LED6.cathode, LED8.anode, R4.Pin_0
  N4: Raspberry_Pi_1.GIPO16, R1.Pin_0
  N5: LED1.cathode, LED2.anode, LED3.cathode, LED7.anode, R4.Pin_1
  N6: LED1.anode, R1.Pin_1, LED2.cathode, LED4.cathode, LED5.anode, LED11.cathode, LED12.anode
  N7: LED3.anode, LED4.anode, LED5.cathode, R2.Pin_1, LED7.cathode, LED9.cathode, LED10.anode
  N8: LED6.anode, R3.Pin_1, LED8.cathode, LED9.anode, LED10.cathode, LED11.anode, LED12.cathode
