# Fritzing sketch led (saved by Fritzing 0.9.3b)
breadboards: 1

parts:
  R1 = Resistor [tolerance=±5% resistance=220 package=THT]
  LED1 = LED - 5mm [color="Red (633nm)" package="5 mm [THT]"]
  Raspberry_Pi_1 = Raspberry Pi 3 [part_number=RPI-3-V1.2]

nets:
  N1: R1.Pin_0, LED1.anode
  N2: R1.Pin_1, Raspberry_Pi_1.GIPO21
  N3: LED1.cathode, Raspberry_Pi_1.GND
